# Fritzing sketch tapuino-modified-pinout (saved by Fritzing 0.9.4)
circuit board: 8.46667cm x 5.64444cm
perfboards: 1

parts:
  J1 = male pin header, 5 pins [form="♂ (male)"]
  J2 = male pin header, 1 pin [form="♂ (male)"]
  Part1 = Arduino Nano (Rev3.0)
  U1 = Optocoupler [package=THT]
  R1 = Resistor [tolerance=±5% resistance=220 package="0805 [SMD]"]
  S2 = Pushbutton [package="[THT]"]
  S3 = Pushbutton [package="[THT]"]
  S4 = Pushbutton [package="[THT]"]
  S5 = Pushbutton [package="[THT]"]
  J6 = microSD header [form="♂ (male)" package=THT]
  J7 = OLED pin header [form="♂ (male)" package=THT]

nets:
  N1: J1.pin1, Part1.D5
  N2: J1.pin2, Part1.D8
  N3: J1.pin3, Part1.D3
  N4: J1.pin4, R1.Pin_1
  VCC: J1.pin5, Part1.5V, J6.Vcc, J7.Vcc
  GND: J2.pin1, Part1.GND, U1.Pin_2, U1.Pin_4, S2.Pin_1, S2.Pin_2, S3.Pin_1, S3.Pin_2, S4.Pin_1, S4.Pin_2, S5.Pin_1, S5.Pin_2, J6.Gnd, J7.Gnd
  N5: Part1.D4, U1.Pin_5
  N6: Part1.D10, J6.CS
  N7: Part1.D11/MOSI, J6.MOSI
  N8: Part1.D12/MISO, J6.MISO
  N9: Part1.A5, J7.SCK
  N10: Part1.A4, J7.SDA
  N11: Part1.A3, S5.Pin_3, S5.Pin_4
  N12: Part1.A2, S4.Pin_3, S4.Pin_4
  N13: Part1.A1, S3.Pin_3, S3.Pin_4
  N14: Part1.A0, S2.Pin_3, S2.Pin_4
  N15: Part1.D13/SCK, J6.SCK
  N16: U1.Pin_1, R1.Pin_0

custom parts:
  microSD header: header for microSD adapter
  OLED pin header: Generic male header
